// Digital circuit immediate.dig as structural Verilog
module immediate (
  input  [31:0] Inst,
  output [31:0] Imm
);

  wire B_type, I_type, J_type, S_type, U_type;

  assign Imm = I_type ? {{21{Inst[31]}}, Inst[30:20]} : 32'bz;  // Driver driver_1
  assign Imm = S_type ? {{21{Inst[31]}}, Inst[30:25], Inst[11:7]} : 32'bz;  // Driver driver_2
  assign Imm = B_type ? {{20{Inst[31]}}, Inst[7], Inst[30:25], Inst[11:8], 1'b0} : 32'bz;  // Driver driver_3
  assign Imm = U_type ? {Inst[31:12], {12{1'b0}}} : 32'bz;  // Driver driver_4
  assign Imm = J_type ? {{12{Inst[31]}}, Inst[19:12], Inst[20], Inst[30:21], 1'b0} : 32'bz;  // Driver driver_5
  PullDown #(.Bits(32)) pulldown_1 (.out(Imm));

  // Other names for the same wires on the sheet: inst_7 = Inst[7]; inst_8_11[3:0] = Inst[11:8];
  //   inst_12_19[7:0] = Inst[19:12]; inst_20 = Inst[20]; inst_21_24[3:0] = Inst[24:21]; inst_25_30[5:0] = Inst[30:25];
  //   inst_31 = Inst[31]

  // Notes on the sheet:
  //   I-type
  //   S-type
  //   B-type
  //   U-type
  //   J-type
endmodule
