// Digital circuit procesador.dig as structural Verilog
module procesador (
);

  wire clock, inst_decoder_1_p2, inst_decoder_1_p3, inst_decoder_1_p4, multiplexer_1_out, pc_jump,
       program_mem_1_p2, reset, rfwren;
  wire [31:0] add_1_s, pc;
  wire [31:3] undriven;

  Multiplexer multiplexer_1 (.sel(pc_jump), .in_0(add_1_s[0]), .out(multiplexer_1_out));  // open: in_1
  // pc pc_1: pin names not known; wires that end beside it: multiplexer_1_out, 1'b1, reset, clock, pc
  // program_mem program_mem_1: pin names not known; wires that end beside it: pc, program_mem_1_p2
  Add #(.Bits(32)) add_1 (.a(pc), .b({undriven, 3'b100}), .c_i(1'b0), .s(add_1_s));  // open: c_o
  // inst_decoder inst_decoder_1: pin names not known; wires that end beside it: program_mem_1_p2, inst_decoder_1_p2, inst_decoder_1_p3, inst_decoder_1_p4
  // registerfile registerfile_1: pin names not known; wires that end beside it: rfwren, inst_decoder_1_p2, inst_decoder_1_p3, inst_decoder_1_p4, clock
  immediate immediate_1 ();  // open: Inst, Imm
  alu alu_1 ();  // open: ALU_ctrl, A, B, Y
  // Pins of 1 and 32 bits meet at add_1_s
  // Pins of 3 and 32 bits meet at {undriven, 3'b100}
endmodule
