// Digital circuit program-mem.dig as structural Verilog
module program_mem (
  input  [31:0] addr,
  output [31:0] inst
);

  wire [1:0] add_1_s, add_2_s, add_3_s;

  Add add_1 (.a(addr[0]), .b(1'b1), .c_i(1'b0), .s(add_1_s[0]));  // open: c_o
  ROM rom_1 (.A(addr[1:0]), .sel(1'b1), .D(inst[24]));
  ROM rom_2 (.A(add_1_s), .sel(1'b1), .D(inst[16]));
  Add add_2 (.a(add_1_s[0]), .b(1'b1), .c_i(1'b0), .s(add_2_s[0]));  // open: c_o
  ROM rom_3 (.A(add_2_s), .sel(1'b1), .D(inst[8]));
  Add add_3 (.a(add_2_s[0]), .b(1'b1), .c_i(1'b0), .s(add_3_s[0]));  // open: c_o
  ROM rom_4 (.A(add_3_s), .sel(1'b1), .D(inst[0]));
  // Pins of 1 and 2 and 24 bits meet at addr[23:0]
  // Pins of 1 and 8 bits meet at inst[31:24]
  // Pins of 1 and 2 bits meet at add_1_s
  // Pins of 1 and 8 bits meet at inst[7:0]
  // Pins of 1 and 8 bits meet at inst[15:8]
  // Pins of 1 and 8 bits meet at inst[23:16]
  // Pins of 1 and 2 bits meet at add_2_s
  // Pins of 1 and 2 bits meet at add_3_s
endmodule
