// Digital circuit registerfile.dig as structural Verilog
module registerfile (
  input  enable,
  input  [4:0] rdAdrs,
  input  [31:0] rdData,
  input  [4:0] rs1Adrs,
  input  [4:0] rs2Adrs,
  input  clock,
  output [31:0] rs1Data,
  output [31:0] rs2Data
);

  wire x0en, x1en, x2en, x3en, x4en, x5en, x6en, x7en, x8en, x9en, x10en, x11en, x12en, x13en, x14en, x15en,
       x16en, x17en, x18en, x19en, x20en, x21en, x22en, x23en, x24en, x25en, x26en, x27en, x28en, x29en,
       x30en, x31en;
  wire [31:0] dataX0, dataX1, dataX2, dataX3, dataX4, dataX5, dataX6, dataX7, dataX8, dataX9, dataX10,
       dataX11, dataX12, dataX13, dataX14, dataX15, dataX16, dataX17, dataX18, dataX19, dataX20, dataX21,
       dataX22, dataX23, dataX24, dataX25, dataX26, dataX27, dataX28, dataX29, dataX30, dataX31;
  wire [31:1] undriven;

  Demultiplexer #(.Selector_Bits(5)) demultiplexer_1 (
    .sel(rdAdrs), .in(enable), .out_0(x0en), .out_1(x1en), .out_2(x2en), .out_3(x3en), .out_4(x4en),
    .out_5(x5en), .out_6(x6en), .out_7(x7en), .out_8(x8en), .out_9(x9en), .out_10(x10en), .out_11(x11en),
    .out_12(x12en), .out_13(x13en), .out_14(x14en), .out_15(x15en), .out_16(x16en), .out_17(x17en),
    .out_18(x18en), .out_19(x19en), .out_20(x20en), .out_21(x21en), .out_22(x22en), .out_23(x23en),
    .out_24(x24en), .out_25(x25en), .out_26(x26en), .out_27(x27en), .out_28(x28en), .out_29(x29en),
    .out_30(x30en), .out_31(x31en));
  Register #(.Bits(32)) X0 (.D({undriven, 1'b0}), .C(clock), .en(x0en), .Q(dataX0));
  Register #(.Bits(32)) X1 (.D(rdData), .C(clock), .en(x1en), .Q(dataX1));
  Register #(.Bits(32)) X2 (.D(rdData), .C(clock), .en(x2en), .Q(dataX2));
  Register #(.Bits(32)) X3 (.D(rdData), .C(clock), .en(x3en), .Q(dataX3));
  Register #(.Bits(32)) X4 (.D(rdData), .C(clock), .en(x4en), .Q(dataX4));
  Register #(.Bits(32)) X5 (.D(rdData), .C(clock), .en(x5en), .Q(dataX5));
  Register #(.Bits(32)) X6 (.D(rdData), .C(clock), .en(x6en), .Q(dataX6));
  Register #(.Bits(32)) X7 (.D(rdData), .C(clock), .en(x7en), .Q(dataX7));
  Register #(.Bits(32)) X8 (.D(rdData), .C(clock), .en(x8en), .Q(dataX8));
  Register #(.Bits(32)) X9 (.D(rdData), .C(clock), .en(x9en), .Q(dataX9));
  Register #(.Bits(32)) X10 (.D(rdData), .C(clock), .en(x10en), .Q(dataX10));
  Register #(.Bits(32)) X11 (.D(rdData), .C(clock), .en(x11en), .Q(dataX11));
  Register #(.Bits(32)) X12 (.D(rdData), .C(clock), .en(x12en), .Q(dataX12));
  Register #(.Bits(32)) X13 (.D(rdData), .C(clock), .en(x13en), .Q(dataX13));
  Register #(.Bits(32)) X14 (.D(rdData), .C(clock), .en(x14en), .Q(dataX14));
  Register #(.Bits(32)) X15 (.D(rdData), .C(clock), .en(x15en), .Q(dataX15));
  Register #(.Bits(32)) X16 (.D(rdData), .C(clock), .en(x16en), .Q(dataX16));
  Register #(.Bits(32)) X17 (.D(rdData), .C(clock), .en(x17en), .Q(dataX17));
  Register #(.Bits(32)) X18 (.D(rdData), .C(clock), .en(x18en), .Q(dataX18));
  Register #(.Bits(32)) X19 (.D(rdData), .C(clock), .en(x19en), .Q(dataX19));
  Register #(.Bits(32)) X20 (.D(rdData), .C(clock), .en(x20en), .Q(dataX20));
  Register #(.Bits(32)) X21 (.D(rdData), .C(clock), .en(x21en), .Q(dataX21));
  Register #(.Bits(32)) X22 (.D(rdData), .C(clock), .en(x22en), .Q(dataX22));
  Register #(.Bits(32)) X23 (.D(rdData), .C(clock), .en(x23en), .Q(dataX23));
  Register #(.Bits(32)) X24 (.D(rdData), .C(clock), .en(x24en), .Q(dataX24));
  Register #(.Bits(32)) X25 (.D(rdData), .C(clock), .en(x25en), .Q(dataX25));
  Register #(.Bits(32)) X26 (.D(rdData), .C(clock), .en(x26en), .Q(dataX26));
  Register #(.Bits(32)) X27 (.D(rdData), .C(clock), .en(x27en), .Q(dataX27));
  Register #(.Bits(32)) X28 (.D(rdData), .C(clock), .en(x28en), .Q(dataX28));
  Register #(.Bits(32)) X29 (.D(rdData), .C(clock), .en(x29en), .Q(dataX29));
  Register #(.Bits(32)) X30 (.D(rdData), .C(clock), .en(x30en), .Q(dataX30));
  Register #(.Bits(32)) X31 (.D(rdData), .C(clock), .en(x31en), .Q(dataX31));
  Multiplexer #(.Selector_Bits(5), .Bits(32)) multiplexer_1 (
    .sel(rs1Adrs), .in_0(dataX0), .in_1(dataX1), .in_2(dataX2), .in_3(dataX3), .in_4(dataX4), .in_5(dataX5),
    .in_6(dataX6), .in_7(dataX7), .in_8(dataX8), .in_9(dataX9), .in_10(dataX10), .in_11(dataX11),
    .in_12(dataX12), .in_13(dataX13), .in_14(dataX14), .in_15(dataX15), .in_16(dataX16), .in_17(dataX17),
    .in_18(dataX18), .in_19(dataX19), .in_20(dataX20), .in_21(dataX21), .in_22(dataX22), .in_23(dataX23),
    .in_24(dataX24), .in_25(dataX25), .in_26(dataX26), .in_27(dataX27), .in_28(dataX28), .in_29(dataX29),
    .in_30(dataX30), .in_31(dataX31), .out(rs1Data));
  Multiplexer #(.Selector_Bits(5), .Bits(32)) multiplexer_2 (
    .sel(rs2Adrs), .in_0(dataX0), .in_1(dataX1), .in_2(dataX2), .in_3(dataX3), .in_4(dataX4), .in_5(dataX5),
    .in_6(dataX6), .in_7(dataX7), .in_8(dataX8), .in_9(dataX9), .in_10(dataX10), .in_11(dataX11),
    .in_12(dataX12), .in_13(dataX13), .in_14(dataX14), .in_15(dataX15), .in_16(dataX16), .in_17(dataX17),
    .in_18(dataX18), .in_19(dataX19), .in_20(dataX20), .in_21(dataX21), .in_22(dataX22), .in_23(dataX23),
    .in_24(dataX24), .in_25(dataX25), .in_26(dataX26), .in_27(dataX27), .in_28(dataX28), .in_29(dataX29),
    .in_30(dataX30), .in_31(dataX31), .out(rs2Data));
  // Pins of 1 and 32 bits meet at {undriven, 1'b0}
endmodule
